# Fritzing sketch Untitled Sketch 2 (saved by Fritzing 0.9.3b)
breadboards: 1

parts:
  부품1 = Arduino Mega 2560 (Rev3)
  7_Segment1 = 7 Segment Display
  R1 = Resistor [tolerance=±5% resistance=220 package=THT]
  R2 = Resistor [tolerance=±5% resistance=220 package=THT]

nets:
  N1: 부품1.D9_PWM, 7_Segment1.Segment_DP
  N2: 부품1.D8_PWM, 7_Segment1.Segment_A
  N3: 부품1.5V, R1.Pin_0, R2.Pin_0
  N4: 부품1.D2_PWM, 7_Segment1.Segment_G
  N5: 부품1.D3_PWM, 7_Segment1.Segment_F
  N6: 부품1.D4_PWM, 7_Segment1.Segment_E
  N7: 부품1.D5_PWM, 7_Segment1.Segment_D
  N8: 부품1.D6_PWM, 7_Segment1.Segment_C
  N9: 부품1.D7_PWM, 7_Segment1.Segment_B
  N10: 7_Segment1.common_anode, R1.Pin_1, R2.Pin_1

custom parts:
  Arduino Mega 2560 (Rev3): The Arduino Mega 2560 is a microcontroller board based on the ATmega2560 (datasheet). It has 54 digital input/output pins (of which 14 can be used as PWM outputs), 16 analog inputs, 4 UARTs (hardware serial ports), a 16 MHz crystal oscillator, a USB connection, a power jack, an ICSP header, and a reset button. It contains everything needed to support the microcontroller; simply connect it to a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
